// Logisim project 8bit_cpu.circ as structural Verilog: 2 circuits, main circuit main
module main (
  input  in_1
);

  wire and_1_out, and_2_out, and_3_out, and_4_out, CLK, clock_1_out, clr, not_1_out;
  wire [1:0] alu_1_out_4;
  wire [2:0] counter_1_q;
  wire [3:0] controlled_buffer_1_out, counter_2_q, or_1_out, pull_resistor_1_node, pull_resistor_2_node,
       register_1_q, register_2_q, register_2_q_2, register_4_q;
  wire [7:0] alu_1_out_5, controlled_buffer_2_out, controlled_buffer_5_out, controlled_buffer_6_out,
       controlled_buffer_7_out, DISP, register_5_q, register_6_q;
  wire [7:4] ram_1_data;
  wire [15:0] rom_1_data;

  assign controlled_buffer_1_out = rom_1_data[14] ? or_1_out : 4'bz;  // Controlled_Buffer controlled_buffer_1
  Register #(.width(4)) register_1 (.D(controlled_buffer_1_out), .Q(register_1_q), .clk(CLK), .clr(clr));  // open: en
  Counter #(.width(3), .max('h4)) counter_1 (
    .Q(counter_1_q), .clk(not_1_out), .clr(clr));  // open: load, D, count, carry
  not not_1 (not_1_out, CLK);
  assign controlled_buffer_2_out = rom_1_data[11] ? {ram_1_data, pull_resistor_1_node} : 8'bz;  // Controlled_Buffer controlled_buffer_2
  assign or_1_out = pull_resistor_1_node | pull_resistor_2_node;  // OR_Gate or_1, 4 bits wide
  Register register_2 (
    .D(controlled_buffer_2_out), .Q({register_2_q, register_2_q_2}), .clk(CLK), .clr(clr));  // open: en
  Pull_Resistor pull_resistor_1 (.node(pull_resistor_1_node));
  Pull_Resistor pull_resistor_2 (.node(pull_resistor_2_node));
  RAM #(.addrWidth(4), .bus("separate")) ram_1 (
    .addr(register_1_q), .din({ram_1_data, pull_resistor_1_node}), .data({ram_1_data, pull_resistor_1_node}),
    .str(rom_1_data[13]), .clk(CLK), .ld(rom_1_data[12]), .clr(and_1_out));  // open: sel
  and and_1 (and_1_out, clr, in_1);
  assign {ram_1_data, pull_resistor_1_node} = rom_1_data[10] ? {register_2_q, register_2_q_2} : 8'bz;  // Controlled_Buffer controlled_buffer_3
  ROM #(.addrWidth(7), .dataWidth(16)) rom_1 (.addr({register_2_q, counter_1_q}), .data(rom_1_data));  // open: sel
  Button button_1 (.out(clr));
  assign pull_resistor_2_node = rom_1_data[15] ? register_4_q : 4'bz;  // Controlled_Buffer controlled_buffer_4
  assign controlled_buffer_5_out = rom_1_data[9] ? {ram_1_data, pull_resistor_1_node} : 8'bz;  // Controlled_Buffer controlled_buffer_5
  assign controlled_buffer_6_out = rom_1_data[8] ? {ram_1_data, pull_resistor_1_node} : 8'bz;  // Controlled_Buffer controlled_buffer_6
  assign controlled_buffer_7_out = rom_1_data[6] ? {ram_1_data, pull_resistor_1_node} : 8'bz;  // Controlled_Buffer controlled_buffer_7
  Register register_3 (.D(controlled_buffer_7_out), .Q(DISP), .clk(CLK), .clr(clr));  // open: en
  Counter #(.width(4), .max('hf)) counter_2 (
    .load(rom_1_data[5]), .D(pull_resistor_1_node), .count(rom_1_data[4]), .Q(counter_2_q), .clk(CLK),
    .clr(clr));  // open: carry
  assign {ram_1_data, pull_resistor_1_node} = rom_1_data[7] ? register_5_q : 8'bz;  // Controlled_Buffer controlled_buffer_8
  or or_2 (CLK, and_2_out, and_3_out, and_4_out);
  and and_2 (and_2_out, clock_1_out, ~rom_1_data[2]);  // AND_Gate
  and and_3 (and_3_out, clock_1_out, ~rom_1_data[1]);  // AND_Gate
  Clock clock_1 (.out(clock_1_out));
  Register #(.width(4)) register_4 (.D(counter_2_q), .Q(register_4_q), .clk(CLK), .clr(clr));  // open: en
  Register register_5 (.D(controlled_buffer_5_out), .Q(register_5_q), .clk(CLK), .clr(clr));  // open: en
  Register register_6 (.D(controlled_buffer_6_out), .Q(register_6_q), .clk(CLK), .clr(clr));  // open: en
  and and_4 (and_4_out, clock_1_out, ~rom_1_data[0]);  // AND_Gate
  assign controlled_buffer_5_out = rom_1_data[3] ? alu_1_out_5 : 8'bz;  // Controlled_Buffer controlled_buffer_9
  ALU alu_1 (
    .in_1(register_5_q), .in_2(register_6_q), .in_3(rom_1_data[2:0]), .out_4(alu_1_out_4), .out_5(alu_1_out_5));
  Register #(.width(2)) register_7 (.D(alu_1_out_4), .clk(CLK), .clr(clr));  // open: en, Q
  Hex_Digit_Display hex_digit_display_1 (.value(DISP[7:4]));  // open: dp
  Hex_Digit_Display hex_digit_display_2 (.value(DISP[3:0]));  // open: dp

  // Notes on the sheet:
  //   MAR
  //   RAM
  //   IR
  //   Control Unit
  //   contents of rom_1 (hex, n*v repeats v):
  //   c000 1810 6*0 c000 1810 4400 1200 4*0 c000 1810 4400 2080 4*0 c000 1810 4400 1100 8 0 0 0 c000 1810
  //   4400 1100 9 0 0 0 c000 1810 4400 1100 a 0 0 0 c000 1810 4400 1100 b 0 0 0 c000 1810 420 5*0 c000
  //   1810 7 5*0 c000 1810 c0 5*0 c000 1810 4400 1100 c 0 0 0 c000 1810 4400 1100 d 0 0 0 c000 1810 4400
  //   1200 e 0 0 0 c000 1810 6*0 c000 1810 6*0 c000 1810
  //   RESET
  //   OutReg
  //   PC
  //   AC
  //   Reg B
  //   ALU
  //   Status Register
endmodule

module ALU (
  input  [7:0] in_1,
  input  [7:0] in_2,
  input  [2:0] in_3,
  output [1:0] out_4,
  output [7:0] out_5
);

  wire [0:0] subtractor_1_bout;
  wire [1:1] adder_1_cout;
  wire [7:0] adder_1_out, and_1_out, divider_1_out, multiplier_1_out, not_1_out, or_1_out, subtractor_1_out;

  Adder adder_1 (.a(in_1), .b(in_2), .out(adder_1_out), .cout(adder_1_cout[1]));  // open: cin
  Subtractor subtractor_1 (.a(in_1), .b(in_2), .out(subtractor_1_out), .bout(subtractor_1_bout[0]));  // open: bin
  Multiplier multiplier_1 (.a(in_1), .b(in_2), .out(multiplier_1_out));  // open: cin, cout
  Divider divider_1 (.a(in_1), .b(in_2), .out(divider_1_out));  // open: upper, rem
  assign or_1_out = in_1 | in_2;  // OR_Gate or_1, 8 bits wide
  assign and_1_out = in_1 & in_2;  // AND_Gate and_1, 8 bits wide
  assign not_1_out = ~in_1;  // NOT_Gate not_1, 8 bits wide
  Multiplexer #(.select(3), .width(2)) multiplexer_1 (
    .in0({adder_1_cout[1], 1'b0}), .in1({1'b0, subtractor_1_bout[0]}), .out(out_4), .sel(in_3));  // open: in2, in3, in4, in5, in6, in7, en
  Multiplexer #(.select(3), .width(8)) multiplexer_2 (
    .in0(adder_1_out), .in1(subtractor_1_out), .in2(multiplier_1_out), .in3(divider_1_out), .in4(or_1_out),
    .in5(and_1_out), .in6(not_1_out), .out(out_5), .sel(in_3));  // open: in7, en

  // Other names for the same wires on the sheet: SEL[2:0] = in_3
endmodule
